# Fritzing sketch sous vide (saved by Fritzing 0.9.2b)
breadboards: 1

parts:
  FTDI_USB_to_Serial = FTDI Basic Programmer
  U3 = DSUN-DC Adapter
  C1 = Electrolytic Capacitor [package="300 mil [THT, electrolytic]"]
  R1 = Resistor [tolerance=±5% resistance=470 package="2512 [SMD]"]
  U5 = 2-Channel 5v Relay Shield [package=relay-2ch5v10a]
  Temperature_probe = DS18B20 1-Wire Temperature Sensor [part_number=DS18B20]
  U4 = DSUN-DC Adapter
  U1 = ESP8266 WiFi Module [part_number=ESP8266]

nets:
  N1: FTDI_USB_to_Serial.RXI, U1.TXD
  N2: FTDI_USB_to_Serial.TXO, U1.RXD
  GND: FTDI_USB_to_Serial.GND, U3.GND_OUT, C1.-, Temperature_probe.GND, U1.GND, U1.GPIO_15
  N3: U3.VCC_IN, U4.VCC_IN
  VDD: U3.VCC_OUT, C1.+, R1.Pin_1, Temperature_probe.VDD, U1.VCC, U1.GPIO_2, U1.CH_PD
  N4: R1.Pin_0, Temperature_probe.DQ, U1.GPIO_14
  N5: U5.VCC, U4.VCC_OUT
  N6: U5.GND, U4.GND_OUT
  N7: U5.IN2, U1.GPIO_13

custom parts:
  DSUN-DC Adapter: DSUN-DC Adapter with variable input/output
  Electrolytic Capacitor: 2200µF electrolytic capacitor
  2-Channel 5v Relay Shield: 2 Channel 5v Relay Shield w. 2x SPD-06VDC-SD-C
  ESP8266 WiFi Module: Generic WiFi Module based on the ESP8266 with onboard PCB antenna and UART communications
